# Fritzing sketch Electronic_Circuit (saved by Fritzing 0.8.5b)
breadboards: 1

parts:
  U1 = NodeMCU V1.0
  R1 = Resistor [tolerance=±5% resistance=10k package=THT]
  R2 = Resistor [tolerance=±5% resistance=10k package=THT]
  RHT1 = Humidity and Temperature Sensor RHT03  # not connected
  J1 = female pin header, 2 pins [form="♀ (female)"]
  J2 = female pin header, 2 pins [form="♀ (female)"]
  J3 = female pin header, 2 pins [form="♀ (female)"]

nets:
  N1: U1.D2, R2.Pin_1
  N2: U1.3V3, R2.Pin_0, J2.pin1, J3.pin1
  N3: U1.GND, R1.Pin_0, J3.pin2
  N4: U1.Vin, J1.pin1
  N5: U1.A0, R1.Pin_1, J1.pin2, J2.pin2

notes:
  1
  6
  Vc
  Vh
  GND
  Vrl

custom parts:
  NodeMCU V1.0: ESP8266 based NodeMCU
